# Fritzing sketch reactionGameRGBLed (saved by Fritzing 0.9.3b)
breadboards: 1

parts:
  LED1 = RGB LED (com. cathode, rgb) [package="5 mm [THT]"]
  LED2 = RGB LED (com. cathode, rgb) [package="5 mm [THT]"]
  S2 = Pushbutton [package="[THT]"]
  S3 = Pushbutton [package="[THT]"]
  S1 = Pushbutton [package="[THT]"]
  Part1 = Arduino Uno (Rev3)
  Squix1 = OLED 0.96" 128x64 I2C SSD1306
  S4 = Pushbutton [package="[THT]"]
  S5 = Pushbutton [package="[THT]"]
  S6 = Pushbutton [package="[THT]"]
  R1 = Resistor [tolerance=±5% resistance=330 package=THT]
  R2 = Resistor [tolerance=±5% resistance=330 package=THT]

nets:
  N1: LED1.red_anode, LED2.red_anode
  N2: LED1.common_cathode, LED2.common_cathode
  N3: LED1.green_anode, R1.Pin_1
  N4: LED1.blue_anode, LED2.blue_anode
  N5: LED2.green_anode, R2.Pin_1
  N6: S2.Pin_1, S2.Pin_2
  GND: S2.Pin_3, S2.Pin_4, S3.Pin_3, S3.Pin_4, S1.Pin_3, S1.Pin_4, Part1.GND, Squix1.GND, S4.Pin_3, S4.Pin_4, S5.Pin_3, S5.Pin_4, S6.Pin_3, S6.Pin_4, R1.Pin_0, R2.Pin_0
  N7: S3.Pin_1, S3.Pin_2
  N8: S1.Pin_1, S1.Pin_2
  5V: Part1.5V, Squix1.VCC
  N9: S4.Pin_1, S4.Pin_2
  N10: S5.Pin_1, S5.Pin_2
  N11: S6.Pin_1, S6.Pin_2
